# Fritzing sketch RFID Project-2 (saved by Fritzing 0.8.7b)
breadboards: 1

parts:
  Part1 = Arduino Mega ADK (Rev3)
  Part2 = RFID-RC522-v2
  Part3 = 4x4 Keypad [part_number=101207]

nets:
  GND: Part1.GND, Part2.GND
  N1: Part1.D9_PWM, Part3.1
  N2: Part1.D8_PWM, Part3.2
  3V3: Part1.3V3, Part2.3.3V
  N3: Part1.D2_PWM, Part3.8
  N4: Part1.D3_PWM, Part3.7
  N5: Part1.D4_PWM, Part3.6
  N6: Part1.D5_PWM, Part3.5
  N7: Part1.D6_PWM, Part3.4
  N8: Part1.D7_PWM, Part3.3
  N9: Part1.D49, Part2.RST
  N10: Part1.D50/MISO, Part2.MISO
  N11: Part1.D51/MOSI, Part2.MOSI
  N12: Part1.D52/SCK, Part2.SCK
  N13: Part1.D53/SS, Part2.SDA

custom parts:
  RFID-RC522-v2: A simple China made RFID-RC522 Reader; do check the pin labels, as this is a MFRC522 based clone.
  4x4 Keypad: Matrix membrane keypad 4x4
